// Logisim project Lavaneko32.circ as structural Verilog: 16 circuits, main circuit Lavaneko
module AddSub (
  input  [31:0] A,
  input  [31:0] B,
  input  SUB,
  output [31:0] RESULT,
  output CARRY,
  output ZERO
);

  wire C1, C2, C3, C4, C5, C6, C7;
  wire [3:0] B0, B1, B2, B3, B4, B5, B6, B7;
  wire [31:0] NOT_B;

  Adder #(.width(4)) adder_1 (.a(A[3:0]), .b(B0), .out(RESULT[3:0]), .cin(SUB), .cout(C1));
  Adder #(.width(4)) adder_2 (.a(A[19:16]), .b(B4), .out(RESULT[19:16]), .cin(C4), .cout(C5));
  assign NOT_B = ~B;  // NOT_Gate not_1, 32 bits wide
  Adder #(.width(4)) adder_3 (.a(A[7:4]), .b(B1), .out(RESULT[7:4]), .cin(C1), .cout(C2));
  Adder #(.width(4)) adder_4 (.a(A[23:20]), .b(B5), .out(RESULT[23:20]), .cin(C5), .cout(C6));
  Multiplexer #(.width(32), .select(1), .enable("false")) multiplexer_1 (
    .in0(B), .in1(NOT_B), .out({B7, B6, B5, B4, B3, B2, B1, B0}), .sel(SUB));
  Comparator #(.width(32), .mode("unsigned")) comparator_1 (.a(RESULT), .b({32{1'b0}}), .eq(ZERO));  // open: gt, lt
  Adder #(.width(4)) adder_5 (.a(A[11:8]), .b(B2), .out(RESULT[11:8]), .cin(C2), .cout(C3));
  Adder #(.width(4)) adder_6 (.a(A[27:24]), .b(B6), .out(RESULT[27:24]), .cin(C6), .cout(C7));
  Adder #(.width(4)) adder_7 (.a(A[15:12]), .b(B3), .out(RESULT[15:12]), .cin(C3), .cout(C4));
  Adder #(.width(4)) adder_8 (.a(A[31:28]), .b(B7), .out(RESULT[31:28]), .cin(C7), .cout(CARRY));

  // Other names for the same wires on the sheet: A0[3:0] = A[3:0]; A1[3:0] = A[7:4]; A2[3:0] = A[11:8];
  //   A3[3:0] = A[15:12]; A4[3:0] = A[19:16]; A5[3:0] = A[23:20]; A6[3:0] = A[27:24]; A7[3:0] = A[31:28];
  //   B_EFFECTIVE[31:0] = {B7, B6, B5, B4, B3, B2, B1, B0}; S0[3:0] = RESULT[3:0]; S1[3:0] = RESULT[7:4];
  //   S2[3:0] = RESULT[11:8]; S3[3:0] = RESULT[15:12]; S4[3:0] = RESULT[19:16]; S5[3:0] = RESULT[23:20];
  //   S6[3:0] = RESULT[27:24]; S7[3:0] = RESULT[31:28]

  // Notes on the sheet:
  //   4-bit adder slices; subtraction = A + complement(B) + 1
  //   Bits 3:0
  //   Bits 19:16
  //   Bits 7:4
  //   Bits 23:20
  //   Bits 11:8
  //   Bits 27:24
  //   Bits 15:12
  //   Bits 31:28
endmodule

module RegisterBank (
  input  CLK,
  input  RESET,
  input  WRITE,
  input  [1:0] DEST,
  input  [1:0] SELECT_A,
  input  [1:0] SELECT_B,
  input  [31:0] DATA,
  output [31:0] READ_A,
  output [31:0] READ_B,
  output [31:0] REG1,
  output [31:0] REG2,
  output [31:0] REG3,
  output [31:0] REG4
);

  wire SELECTED0, SELECTED1, SELECTED2, SELECTED3, WE0, WE1, WE2, WE3;

  Comparator #(.width(2), .mode("unsigned")) comparator_1 (.a(DEST), .b(2'b00), .eq(SELECTED0));  // open: gt, lt
  Comparator #(.width(2), .mode("unsigned")) comparator_2 (.a(DEST), .b(2'b01), .eq(SELECTED1));  // open: gt, lt
  Comparator #(.width(2), .mode("unsigned")) comparator_3 (.a(DEST), .b(2'b10), .eq(SELECTED2));  // open: gt, lt
  Comparator #(.width(2), .mode("unsigned")) comparator_4 (.a(DEST), .b(2'b11), .eq(SELECTED3));  // open: gt, lt
  Multiplexer #(.width(32), .select(2), .enable("false")) multiplexer_1 (
    .in0(REG1), .in1(REG2), .in2(REG3), .in3(REG4), .out(READ_A), .sel(SELECT_A));
  and and_1 (WE0, SELECTED0, WRITE);
  and and_2 (WE1, SELECTED1, WRITE);
  and and_3 (WE2, SELECTED2, WRITE);
  and and_4 (WE3, SELECTED3, WRITE);
  Register #(.width(32), .trigger("falling"), .showLabel("true")) u_REG1 (
    .D(DATA), .en(WE0), .Q(REG1), .clk(CLK), .clr(RESET));
  Register #(.width(32), .trigger("falling"), .showLabel("true")) u_REG2 (
    .D(DATA), .en(WE1), .Q(REG2), .clk(CLK), .clr(RESET));
  Register #(.width(32), .trigger("falling"), .showLabel("true")) u_REG3 (
    .D(DATA), .en(WE2), .Q(REG3), .clk(CLK), .clr(RESET));
  Register #(.width(32), .trigger("falling"), .showLabel("true")) u_REG4 (
    .D(DATA), .en(WE3), .Q(REG4), .clk(CLK), .clr(RESET));
  Multiplexer #(.width(32), .select(2), .enable("false")) multiplexer_2 (
    .in0(REG1), .in1(REG2), .in2(REG3), .in3(REG4), .out(READ_B), .sel(SELECT_B));

  // Notes on the sheet:
  //   Independent read A / read B / write destination; falling-edge commit
endmodule

module ProgramCounter (
  input  CLK,
  input  RESET,
  input  ENABLE,
  input  JUMP,
  input  [15:0] TARGET,
  output [15:0] PC
);

  wire WRAP;
  wire [15:0] NEXT, PC_D;

  Adder #(.width(16)) adder_1 (.a(PC), .b(16'h1), .out(NEXT), .cin(1'b0), .cout(WRAP));
  Multiplexer #(.width(16), .select(1), .enable("false")) multiplexer_1 (
    .in0(NEXT), .in1(TARGET), .out(PC_D), .sel(JUMP));
  Register #(.width(16), .trigger("falling"), .showLabel("true")) u_PC (
    .D(PC_D), .en(ENABLE), .Q(PC), .clk(CLK), .clr(RESET));
endmodule

module ProgramROM (
  input  [15:0] ADDRESS,
  output [47:0] INSTRUCTION
);

  ROM #(.addrWidth(16), .dataWidth(48)) PROGRAM (.addr(ADDRESS), .data(INSTRUCTION));

  // Notes on the sheet:
  //   Program words = low 16 control bits + full-width immediate
  //   Edit PROGRAM contents to load your own reconstructed control words
  //   contents of PROGRAM (hex, n*v repeats v):
  //   a0022 30422 4982 6d83 200208 200406 5281 a8000 dead0022 40 50022 422 10c22 5482 4383 128000 d0010 40
  //   210108 210806 fffffff90022 30422 9c1 cc5 300208 310308 9c3 cc5 320208 330308 ffffffff0022 8c0 9c2
  //   8c4 422 9c2 cc6 340308 800000000022 ffffffff0422 9c3 cc6 350308 70022 fffffffd0422 9c3 cc5 40
endmodule

module Control (
  input  [47:0] INSTRUCTION,
  output SUB,
  output REG_WRITE,
  output LOAD,
  output STORE,
  output JUMP,
  output B_ZERO,
  output HALT,
  output A_REG,
  output [1:0] SELECT_B,
  output [1:0] DEST,
  output [1:0] SELECT_A,
  output FLAGS_WRITE,
  output JZ,
  output [31:0] IMMEDIATE,
  output MD,
  output MD_SIGNED,
  output MD_DIV,
  output [1:0] WB_SELECT
);

  wire EXT, EXT_0, EXT_1, EXT_2, EXT_3, EXT_4, EXT_5, EXT_6, EXT_WRITE, IS_MUL, LEGACY, LEGACY_WRITE,
       SELECT_LO;
  wire [7:0] OPCODE;

  and and_1 (EXT, INSTRUCTION[6], INSTRUCTION[7]);
  not not_1 (LEGACY, EXT);
  Bit_Extender #(.in_width(48), .out_width(8), .\type ("zero")) bit_extender_1 (.in(INSTRUCTION), .out(OPCODE));
  and and_2 (LEGACY_WRITE, INSTRUCTION[1], LEGACY);
  and and_3 (LOAD, INSTRUCTION[2], LEGACY);
  and and_4 (STORE, INSTRUCTION[3], LEGACY);
  and and_5 (JUMP, INSTRUCTION[4], LEGACY);
  and and_6 (HALT, INSTRUCTION[6], LEGACY);
  and and_7 (FLAGS_WRITE, INSTRUCTION[14], LEGACY);
  and and_8 (JZ, INSTRUCTION[15], LEGACY);
  Comparator #(.width(8), .mode("unsigned")) comparator_1 (.a(OPCODE), .b(8'hc0), .eq(EXT_0));  // open: gt, lt
  Comparator #(.width(8), .mode("unsigned")) comparator_2 (.a(OPCODE), .b(8'hc1), .eq(EXT_1));  // open: gt, lt
  Comparator #(.width(8), .mode("unsigned")) comparator_3 (.a(OPCODE), .b(8'hc2), .eq(EXT_2));  // open: gt, lt
  Comparator #(.width(8), .mode("unsigned")) comparator_4 (.a(OPCODE), .b(8'hc3), .eq(EXT_3));  // open: gt, lt
  Comparator #(.width(8), .mode("unsigned")) comparator_5 (.a(OPCODE), .b(8'hc4), .eq(EXT_4));  // open: gt, lt
  Comparator #(.width(8), .mode("unsigned")) comparator_6 (.a(OPCODE), .b(8'hc5), .eq(EXT_5));  // open: gt, lt
  Comparator #(.width(8), .mode("unsigned")) comparator_7 (.a(OPCODE), .b(8'hc6), .eq(EXT_6));  // open: gt, lt
  or or_1 (IS_MUL, EXT_0, EXT_1);
  or or_2 (MD_DIV, EXT_2, EXT_3);
  or or_3 (MD, IS_MUL, MD_DIV);
  or or_4 (MD_SIGNED, EXT_1, EXT_3);
  or or_5 (SELECT_LO, MD, EXT_4);
  or or_6 (WB_SELECT[0], SELECT_LO, EXT_6);
  or or_7 (WB_SELECT[1], EXT_5, EXT_6);
  or or_8 (EXT_WRITE, WB_SELECT[0], WB_SELECT[1]);
  or or_9 (REG_WRITE, LEGACY_WRITE, EXT_WRITE);

  assign A_REG = INSTRUCTION[7];
  assign B_ZERO = INSTRUCTION[5];
  assign DEST = INSTRUCTION[11:10];
  assign IMMEDIATE = INSTRUCTION[47:16];
  assign SELECT_A = INSTRUCTION[13:12];
  assign SELECT_B = INSTRUCTION[9:8];
  assign SUB = INSTRUCTION[0];

  // Other names for the same wires on the sheet: RAW_REG_WRITE = INSTRUCTION[1]; RAW_LOAD = INSTRUCTION[2];
  //   RAW_STORE = INSTRUCTION[3]; RAW_JUMP = INSTRUCTION[4]; RAW_HALT = INSTRUCTION[6];
  //   RAW_FLAGS_WRITE = INSTRUCTION[14]; RAW_JZ = INSTRUCTION[15]; WB_BIT_0 = WB_SELECT[0]; WB_BIT_1 = WB_SELECT[1]
endmodule

module DataRAM (
  input  CLK,
  input  RESET,
  input  WRITE,
  input  [15:0] ADDRESS,
  input  [31:0] DATA,
  output [31:0] READ
);

  RAM #(.addrWidth(16), .dataWidth(32), .databus("bibus"), .enables("line"), .line("single"), .trigger("falling"), .clearpin("true")) DATA_RAM (
    .addr(ADDRESS), .we(WRITE), .clk(CLK), .din(DATA), .dout(READ), .clr(RESET));
endmodule

module Sequencer (
  input  CLK,
  input  RESET,
  input  HALT,
  input  REG_WRITE,
  input  STORE,
  input  FLAGS_WRITE,
  input  JUMP,
  input  JZ,
  input  ALU_ZERO,
  input  ALU_CARRY,
  input  MD,
  input  CORE_DONE,
  input  MD_OK,
  output ENABLE,
  output FETCH,
  output WRITE,
  output MEM_WRITE,
  output BRANCH,
  output Z,
  output C,
  output BUSY,
  output MD_START,
  output MD_ACK
);

  wire ALLOW_WRITE, CAN_COMMIT, FLAG_ENABLE, MD_WAITING, NOT_BUSY, NOT_DONE, NOT_HALT, NOT_MD, NOT_RESET,
       RUN, START_REQUEST, TAKEN_Z, WAIT_NEXT, WRITE_REQUEST;

  not not_1 (NOT_HALT, HALT);
  not not_2 (NOT_RESET, RESET);
  not not_3 (NOT_BUSY, BUSY);
  not not_4 (NOT_MD, MD);
  not not_5 (NOT_DONE, CORE_DONE);
  and and_1 (RUN, NOT_HALT, NOT_RESET);
  and and_2 (FETCH, RUN, NOT_BUSY);
  and and_3 (START_REQUEST, MD, NOT_BUSY);
  and and_4 (MD_START, START_REQUEST, RUN);
  and and_5 (MD_WAITING, MD, BUSY);
  and and_6 (MD_ACK, MD_WAITING, CORE_DONE);
  or or_1 (CAN_COMMIT, NOT_MD, MD_ACK);
  and and_7 (ENABLE, CAN_COMMIT, RUN);
  or or_2 (ALLOW_WRITE, NOT_MD, MD_OK);
  and and_8 (WRITE_REQUEST, ENABLE, REG_WRITE);
  and and_9 (WRITE, WRITE_REQUEST, ALLOW_WRITE);
  and and_10 (MEM_WRITE, ENABLE, STORE);
  and and_11 (FLAG_ENABLE, ENABLE, FLAGS_WRITE);
  and and_12 (TAKEN_Z, JZ, Z);
  or or_3 (BRANCH, JUMP, TAKEN_Z);
  and and_13 (WAIT_NEXT, MD, NOT_DONE);
  Register #(.width(1), .trigger("falling"), .showLabel("true")) u_BUSY (
    .D(WAIT_NEXT), .en(1'b1), .Q(BUSY), .clk(CLK), .clr(RESET));
  Register #(.width(1), .trigger("falling"), .showLabel("true")) u_Z (
    .D(ALU_ZERO), .en(FLAG_ENABLE), .Q(Z), .clk(CLK), .clr(RESET));
  Register #(.width(1), .trigger("falling"), .showLabel("true")) u_C (
    .D(ALU_CARRY), .en(FLAG_ENABLE), .Q(C), .clk(CLK), .clr(RESET));
endmodule

module SliceArithmetic32 (
  input  [31:0] A,
  input  [31:0] B,
  input  SUB,
  output [31:0] RESULT,
  output CARRY
);

  wire C_1, C_2, C_3, C_4, C_5, C_6, C_7;
  wire [3:0] A_0, A_1, A_2, A_3, A_4, A_5, A_6, A_7, B_0, B_1, B_2, B_3, B_4, B_5, B_6, B_7;
  wire [31:0] B_NOT, B_PAD, RESULT_PAD;

  Bit_Extender #(.in_width(32), .out_width(32), .\type ("zero")) bit_extender_1 (
    .in(A), .out({A_7, A_6, A_5, A_4, A_3, A_2, A_1, A_0}));
  Adder #(.width(4)) adder_1 (.a(A_3), .b(B_3), .out(RESULT_PAD[15:12]), .cin(C_3), .cout(C_4));
  Bit_Extender #(.in_width(32), .out_width(32), .\type ("zero")) bit_extender_2 (.in(RESULT_PAD), .out(RESULT));
  Bit_Extender #(.in_width(32), .out_width(32), .\type ("zero")) bit_extender_3 (.in(B), .out(B_PAD));
  Adder #(.width(4)) adder_2 (.a(A_4), .b(B_4), .out(RESULT_PAD[19:16]), .cin(C_4), .cout(C_5));
  assign B_NOT = ~B_PAD;  // NOT_Gate not_1, 32 bits wide
  Adder #(.width(4)) adder_3 (.a(A_0), .b(B_0), .out(RESULT_PAD[3:0]), .cin(SUB), .cout(C_1));
  Adder #(.width(4)) adder_4 (.a(A_5), .b(B_5), .out(RESULT_PAD[23:20]), .cin(C_5), .cout(C_6));
  Multiplexer #(.width(32), .select(1), .enable("false")) multiplexer_1 (
    .in0(B_PAD), .in1(B_NOT), .out({B_7, B_6, B_5, B_4, B_3, B_2, B_1, B_0}), .sel(SUB));
  Adder #(.width(4)) adder_5 (.a(A_1), .b(B_1), .out(RESULT_PAD[7:4]), .cin(C_1), .cout(C_2));
  Adder #(.width(4)) adder_6 (.a(A_6), .b(B_6), .out(RESULT_PAD[27:24]), .cin(C_6), .cout(C_7));
  Adder #(.width(4)) adder_7 (.a(A_2), .b(B_2), .out(RESULT_PAD[11:8]), .cin(C_2), .cout(C_3));
  Adder #(.width(4)) adder_8 (.a(A_7), .b(B_7), .out(RESULT_PAD[31:28]), .cin(C_7), .cout(CARRY));

  // Other names for the same wires on the sheet: A_PAD[31:0] = {A_7, A_6, A_5, A_4, A_3, A_2, A_1, A_0};
  //   B_EFFECTIVE[31:0] = {B_7, B_6, B_5, B_4, B_3, B_2, B_1, B_0}; S_0[3:0] = RESULT_PAD[3:0];
  //   S_1[3:0] = RESULT_PAD[7:4]; S_2[3:0] = RESULT_PAD[11:8]; S_3[3:0] = RESULT_PAD[15:12];
  //   S_4[3:0] = RESULT_PAD[19:16]; S_5[3:0] = RESULT_PAD[23:20]; S_6[3:0] = RESULT_PAD[27:24];
  //   S_7[3:0] = RESULT_PAD[31:28]
endmodule

module SliceArithmetic33 (
  input  [32:0] A,
  input  [32:0] B,
  input  SUB,
  output [32:0] RESULT,
  output CARRY
);

  wire C_1, C_2, C_3, C_4, C_5, C_6, C_7, C_8;
  wire [3:0] A_0, A_1, A_2, A_3, A_4, A_5, A_6, A_7, A_8, B_0, B_1, B_2, B_3, B_4, B_5, B_6, B_7, B_8;
  wire [35:0] B_NOT, B_PAD, RESULT_PAD;

  assign {A_8, A_7, A_6, A_5, A_4, A_3, A_2, A_1, A_0} = {{3{1'b0}}, A};  // Bit_Extender bit_extender_1
  Adder #(.width(4)) adder_1 (.a(A_3), .b(B_3), .out(RESULT_PAD[15:12]), .cin(C_3), .cout(C_4));
  Adder #(.width(4)) adder_2 (.a(A_8), .b(B_8), .out(RESULT_PAD[35:32]), .cin(C_8), .cout(CARRY));
  assign B_PAD = {{3{1'b0}}, B};  // Bit_Extender bit_extender_2
  Adder #(.width(4)) adder_3 (.a(A_4), .b(B_4), .out(RESULT_PAD[19:16]), .cin(C_4), .cout(C_5));
  Bit_Extender #(.in_width(36), .out_width(33), .\type ("zero")) bit_extender_3 (.in(RESULT_PAD), .out(RESULT));
  assign B_NOT = ~B_PAD;  // NOT_Gate not_1, 36 bits wide
  Adder #(.width(4)) adder_4 (.a(A_0), .b(B_0), .out(RESULT_PAD[3:0]), .cin(SUB), .cout(C_1));
  Adder #(.width(4)) adder_5 (.a(A_5), .b(B_5), .out(RESULT_PAD[23:20]), .cin(C_5), .cout(C_6));
  Multiplexer #(.width(36), .select(1), .enable("false")) multiplexer_1 (
    .in0(B_PAD), .in1(B_NOT), .out({B_8, B_7, B_6, B_5, B_4, B_3, B_2, B_1, B_0}), .sel(SUB));
  Adder #(.width(4)) adder_6 (.a(A_1), .b(B_1), .out(RESULT_PAD[7:4]), .cin(C_1), .cout(C_2));
  Adder #(.width(4)) adder_7 (.a(A_6), .b(B_6), .out(RESULT_PAD[27:24]), .cin(C_6), .cout(C_7));
  Adder #(.width(4)) adder_8 (.a(A_2), .b(B_2), .out(RESULT_PAD[11:8]), .cin(C_2), .cout(C_3));
  Adder #(.width(4)) adder_9 (.a(A_7), .b(B_7), .out(RESULT_PAD[31:28]), .cin(C_7), .cout(C_8));

  // Other names for the same wires on the sheet: A_PAD[35:0] = {A_8, A_7, A_6, A_5, A_4, A_3, A_2, A_1, A_0};
  //   B_EFFECTIVE[35:0] = {B_8, B_7, B_6, B_5, B_4, B_3, B_2, B_1, B_0}; S_0[3:0] = RESULT_PAD[3:0];
  //   S_1[3:0] = RESULT_PAD[7:4]; S_2[3:0] = RESULT_PAD[11:8]; S_3[3:0] = RESULT_PAD[15:12];
  //   S_4[3:0] = RESULT_PAD[19:16]; S_5[3:0] = RESULT_PAD[23:20]; S_6[3:0] = RESULT_PAD[27:24];
  //   S_7[3:0] = RESULT_PAD[31:28]; S_8[3:0] = RESULT_PAD[35:32]
endmodule

module SliceArithmetic64 (
  input  [63:0] A,
  input  [63:0] B,
  input  SUB,
  output [63:0] RESULT,
  output CARRY
);

  wire C_1, C_2, C_3, C_4, C_5, C_6, C_7, C_8, C_9, C_10, C_11, C_12, C_13, C_14, C_15;
  wire [3:0] A_0, A_1, A_2, A_3, A_4, A_5, A_6, A_7, A_8, A_9, A_10, A_11, A_12, A_13, A_14, A_15, B_0, B_1,
       B_2, B_3, B_4, B_5, B_6, B_7, B_8, B_9, B_10, B_11, B_12, B_13, B_14, B_15;
  wire [63:0] B_NOT, B_PAD, RESULT_PAD;

  Bit_Extender #(.in_width(64), .out_width(64), .\type ("zero")) bit_extender_1 (
    .in(A), .out({A_15, A_14, A_13, A_12, A_11, A_10, A_9, A_8, A_7, A_6, A_5, A_4, A_3, A_2, A_1, A_0}));
  Adder #(.width(4)) adder_1 (.a(A_3), .b(B_3), .out(RESULT_PAD[15:12]), .cin(C_3), .cout(C_4));
  Adder #(.width(4)) adder_2 (.a(A_8), .b(B_8), .out(RESULT_PAD[35:32]), .cin(C_8), .cout(C_9));
  Adder #(.width(4)) adder_3 (.a(A_13), .b(B_13), .out(RESULT_PAD[55:52]), .cin(C_13), .cout(C_14));
  Bit_Extender #(.in_width(64), .out_width(64), .\type ("zero")) bit_extender_2 (.in(B), .out(B_PAD));
  Adder #(.width(4)) adder_4 (.a(A_4), .b(B_4), .out(RESULT_PAD[19:16]), .cin(C_4), .cout(C_5));
  Adder #(.width(4)) adder_5 (.a(A_9), .b(B_9), .out(RESULT_PAD[39:36]), .cin(C_9), .cout(C_10));
  Adder #(.width(4)) adder_6 (.a(A_14), .b(B_14), .out(RESULT_PAD[59:56]), .cin(C_14), .cout(C_15));
  assign B_NOT = ~B_PAD;  // NOT_Gate not_1, 64 bits wide
  Adder #(.width(4)) adder_7 (.a(A_0), .b(B_0), .out(RESULT_PAD[3:0]), .cin(SUB), .cout(C_1));
  Adder #(.width(4)) adder_8 (.a(A_5), .b(B_5), .out(RESULT_PAD[23:20]), .cin(C_5), .cout(C_6));
  Adder #(.width(4)) adder_9 (.a(A_10), .b(B_10), .out(RESULT_PAD[43:40]), .cin(C_10), .cout(C_11));
  Adder #(.width(4)) adder_10 (.a(A_15), .b(B_15), .out(RESULT_PAD[63:60]), .cin(C_15), .cout(CARRY));
  Multiplexer #(.width(64), .select(1), .enable("false")) multiplexer_1 (
    .in0(B_PAD), .in1(B_NOT),
    .out({B_15, B_14, B_13, B_12, B_11, B_10, B_9, B_8, B_7, B_6, B_5, B_4, B_3, B_2, B_1, B_0}), .sel(SUB));
  Adder #(.width(4)) adder_11 (.a(A_1), .b(B_1), .out(RESULT_PAD[7:4]), .cin(C_1), .cout(C_2));
  Adder #(.width(4)) adder_12 (.a(A_6), .b(B_6), .out(RESULT_PAD[27:24]), .cin(C_6), .cout(C_7));
  Adder #(.width(4)) adder_13 (.a(A_11), .b(B_11), .out(RESULT_PAD[47:44]), .cin(C_11), .cout(C_12));
  Bit_Extender #(.in_width(64), .out_width(64), .\type ("zero")) bit_extender_3 (.in(RESULT_PAD), .out(RESULT));
  Adder #(.width(4)) adder_14 (.a(A_2), .b(B_2), .out(RESULT_PAD[11:8]), .cin(C_2), .cout(C_3));
  Adder #(.width(4)) adder_15 (.a(A_7), .b(B_7), .out(RESULT_PAD[31:28]), .cin(C_7), .cout(C_8));
  Adder #(.width(4)) adder_16 (.a(A_12), .b(B_12), .out(RESULT_PAD[51:48]), .cin(C_12), .cout(C_13));

  // Other names for the same wires on the sheet: A_PAD[63:0] = {A_15, A_14, A_13, A_12, A_11, A_10, A_9, A_8, A_7, A_6, A_5, A_4, A_3, A_2, A_1, A_0};
  //   B_EFFECTIVE[63:0] = {B_15, B_14, B_13, B_12, B_11, B_10, B_9, B_8, B_7, B_6, B_5, B_4, B_3, B_2, B_1, B_0};
  //   S_0[3:0] = RESULT_PAD[3:0]; S_1[3:0] = RESULT_PAD[7:4]; S_2[3:0] = RESULT_PAD[11:8];
  //   S_3[3:0] = RESULT_PAD[15:12]; S_4[3:0] = RESULT_PAD[19:16]; S_5[3:0] = RESULT_PAD[23:20];
  //   S_6[3:0] = RESULT_PAD[27:24]; S_7[3:0] = RESULT_PAD[31:28]; S_8[3:0] = RESULT_PAD[35:32];
  //   S_9[3:0] = RESULT_PAD[39:36]; S_10[3:0] = RESULT_PAD[43:40]; S_11[3:0] = RESULT_PAD[47:44];
  //   S_12[3:0] = RESULT_PAD[51:48]; S_13[3:0] = RESULT_PAD[55:52]; S_14[3:0] = RESULT_PAD[59:56];
  //   S_15[3:0] = RESULT_PAD[63:60]
endmodule

module ConditionalNegate32 (
  input  [31:0] VALUE,
  input  NEG,
  output [31:0] RESULT
);

  wire UNUSED_CARRY;
  wire [31:0] NEGATED;

  SliceArithmetic32 slicearithmetic32_1 (.A({32{1'b0}}), .B(VALUE), .SUB(1'b1), .RESULT(NEGATED), .CARRY(UNUSED_CARRY));
  Multiplexer #(.width(32), .select(1), .enable("false")) multiplexer_1 (
    .in0(VALUE), .in1(NEGATED), .out(RESULT), .sel(NEG));
endmodule

module ConditionalNegate64 (
  input  [63:0] VALUE,
  input  NEG,
  output [63:0] RESULT
);

  wire UNUSED_CARRY;
  wire [63:0] NEGATED;

  SliceArithmetic64 slicearithmetic64_1 (.A({64{1'b0}}), .B(VALUE), .SUB(1'b1), .RESULT(NEGATED), .CARRY(UNUSED_CARRY));
  Multiplexer #(.width(64), .select(1), .enable("false")) multiplexer_1 (
    .in0(VALUE), .in1(NEGATED), .out(RESULT), .sel(NEG));
endmodule

module MultiplyUnit (
  input  CLK,
  input  RESET,
  input  START,
  input  ACK,
  input  SIGNED,
  input  [31:0] A,
  input  [31:0] B,
  output BUSY,
  output DONE,
  output [31:0] LO,
  output [31:0] HI,
  output [1:0] ERROR
);

  wire ACCEPT, BEGIN_RUN, BUSY_NEXT, CONTINUE_RUN, COUNT_WRAP, DONE_NEXT, ERROR_FINISH, FINISH, HOLD_DONE,
       IDLE, ITERATION_FINISH, LAST, NEG_A, NEG_B, NEG_RESULT, NO_INITIAL_ERROR, NOT_ACK, NOT_BUSY, NOT_DONE,
       NOT_LAST, REMAINDER_NEGATIVE, RESULT_NEGATIVE, STEP_ENABLE;
  wire [4:0] COUNT, COUNT_NEXT, COUNT_PLUS;
  wire [31:0] ABS_A, ABS_B, ADDEND, H, H_NEXT, H_SHIFT, MULTIPLICAND, PRODUCT_UNSIGNED, Q_NEXT;
  wire [31:31] Q_SHIFT;

  ConditionalNegate32 conditionalnegate32_1 (.VALUE(A), .NEG(NEG_A), .RESULT(ABS_A));
  not not_1 (NOT_BUSY, BUSY);
  Register #(.width(1), .trigger("falling"), .showLabel("true")) u_RESULT_NEGATIVE (
    .D(NEG_RESULT), .en(ACCEPT), .Q(RESULT_NEGATIVE), .clk(CLK), .clr(RESET));
  Multiplexer #(.width(32), .select(1), .enable("false")) multiplexer_1 (
    .in0({32{1'b0}}), .in1(MULTIPLICAND), .out(ADDEND), .sel(PRODUCT_UNSIGNED[0]));
  Multiplexer #(.width(32), .select(1), .enable("false")) multiplexer_2 (
    .in0(H_SHIFT), .in1({32{1'b0}}), .out(H_NEXT), .sel(ACCEPT));
  ConditionalNegate64 conditionalnegate64_1 (.VALUE({H, PRODUCT_UNSIGNED}), .NEG(RESULT_NEGATIVE), .RESULT({HI, LO}));
  Comparator #(.width(5), .mode("unsigned")) comparator_1 (.a(COUNT), .b({5{1'b1}}), .eq(LAST));  // open: gt, lt
  not not_2 (NO_INITIAL_ERROR, 1'b0);
  and and_1 (ERROR_FINISH, ACCEPT, 1'b0);
  or or_1 (DONE_NEXT, FINISH, HOLD_DONE);
  not not_3 (NOT_DONE, DONE);
  Register #(.width(1), .trigger("falling"), .showLabel("true")) u_REMAINDER_NEGATIVE (
    .D(NEG_A), .en(ACCEPT), .Q(REMAINDER_NEGATIVE), .clk(CLK), .clr(RESET));
  SliceArithmetic32 slicearithmetic32_1 (
    .A(H), .B(ADDEND), .SUB(1'b0), .RESULT({H_SHIFT[30:0], Q_SHIFT[31]}), .CARRY(H_SHIFT[31]));
  Multiplexer #(.width(32), .select(1), .enable("false")) multiplexer_3 (
    .in0({Q_SHIFT[31], PRODUCT_UNSIGNED[31:1]}), .in1(ABS_B), .out(Q_NEXT), .sel(ACCEPT));
  Adder #(.width(5)) adder_1 (.a(COUNT), .b(5'b00001), .out(COUNT_PLUS), .cin(1'b0), .cout(COUNT_WRAP));
  and and_2 (BEGIN_RUN, ACCEPT, NO_INITIAL_ERROR);
  and and_3 (ITERATION_FINISH, BUSY, LAST);
  Register #(.width(1), .trigger("falling"), .showLabel("true")) u_DONE (
    .D(DONE_NEXT), .en(1'b1), .Q(DONE), .clk(CLK), .clr(RESET));
  and and_4 (NEG_B, SIGNED, B[31]);
  and and_5 (IDLE, NOT_BUSY, NOT_DONE);
  Register #(.width(32), .trigger("falling"), .showLabel("true")) u_H (
    .D(H_NEXT), .en(STEP_ENABLE), .Q(H), .clk(CLK), .clr(RESET));
  Multiplexer #(.width(5), .select(1), .enable("false")) multiplexer_4 (
    .in0(COUNT_PLUS), .in1({5{1'b0}}), .out(COUNT_NEXT), .sel(ACCEPT));
  and and_6 (CONTINUE_RUN, BUSY, NOT_LAST);
  or or_2 (FINISH, ERROR_FINISH, ITERATION_FINISH);
  ConditionalNegate32 conditionalnegate32_2 (.VALUE(B), .NEG(NEG_B), .RESULT(ABS_B));
  and and_7 (ACCEPT, START, IDLE);
  Register #(.width(32), .trigger("falling"), .showLabel("true")) u_MULTIPLICAND (
    .D(ABS_A), .en(ACCEPT), .Q(MULTIPLICAND), .clk(CLK), .clr(RESET));
  Register #(.width(32), .trigger("falling"), .showLabel("true")) Q (
    .D(Q_NEXT), .en(STEP_ENABLE), .Q(PRODUCT_UNSIGNED), .clk(CLK), .clr(RESET));
  Register #(.width(5), .trigger("falling"), .showLabel("true")) u_COUNT (
    .D(COUNT_NEXT), .en(STEP_ENABLE), .Q(COUNT), .clk(CLK), .clr(RESET));
  or or_3 (BUSY_NEXT, BEGIN_RUN, CONTINUE_RUN);
  not not_4 (NOT_ACK, ACK);
  and and_8 (NEG_A, SIGNED, A[31]);
  // XOR_Gate #(.width(1)) xor_1: pin names not known; wires that end beside it: NEG_A, NEG_B, NEG_RESULT
  or or_4 (STEP_ENABLE, ACCEPT, BUSY);
  not not_5 (NOT_LAST, LAST);
  Register #(.width(1), .trigger("falling"), .showLabel("true")) u_BUSY (
    .D(BUSY_NEXT), .en(1'b1), .Q(BUSY), .clk(CLK), .clr(RESET));
  and and_9 (HOLD_DONE, DONE, NOT_ACK);

  assign ERROR = 2'b00;

  // Other names for the same wires on the sheet: A_LOW[30:0] = A[30:0]; A_SIGN = A[31]; B_LOW[30:0] = B[30:0];
  //   B_SIGN = B[31]; SUM[31:0] = {H_SHIFT[30:0], Q_SHIFT[31]}; SUM_UPPER[30:0] = H_SHIFT[30:0];
  //   SUM_CARRY = H_SHIFT[31]; PRODUCT_SIGNED[63:0] = {HI, LO}; Q[31:0] = PRODUCT_UNSIGNED;
  //   Q_BIT = PRODUCT_UNSIGNED[0]; Q_SHIFT[30:0] = PRODUCT_UNSIGNED[31:1]; Q_UPPER[30:0] = PRODUCT_UNSIGNED[31:1];
  //   PRODUCT_UNSIGNED[63:32] = H; SUM_BIT = Q_SHIFT[31]
endmodule

module DivideUnit (
  input  CLK,
  input  RESET,
  input  START,
  input  ACK,
  input  SIGNED,
  input  [31:0] A,
  input  [31:0] B,
  output BUSY,
  output DONE,
  output [31:0] LO,
  output [31:0] HI,
  output [1:0] ERROR
);

  wire A_IS_MIN, ACCEPT, B_IS_MINUS_ONE, BEGIN_RUN, BUSY_NEXT, CONTINUE_RUN, COUNT_WRAP, DIV_ZERO, DONE_NEXT,
       ENOUGH, ERROR_FINISH, FINISH, HAS_ERROR, HOLD_DONE, IDLE, INITIAL_ERROR, ITERATION_FINISH, LAST,
       NEG_A, NEG_B, NEG_RESULT, NO_INITIAL_ERROR, NOT_ACK, NOT_BUSY, NOT_DONE, NOT_LAST, OVERFLOW_PAIR,
       REMAINDER_NEGATIVE, RESULT_NEGATIVE, STEP_ENABLE;
  wire [1:1] ERROR_INPUT;
  wire [4:0] COUNT, COUNT_NEXT, COUNT_PLUS;
  wire [31:0] ABS_A, ABS_B, DIVISOR, Q, Q_NEXT, QUOTIENT_SIGNED, REMAINDER_SIGNED;
  wire [32:0] DIVISOR_EXT, R, R_NEXT, R_STEP, TRIAL;

  ConditionalNegate32 conditionalnegate32_1 (.VALUE(A), .NEG(NEG_A), .RESULT(ABS_A));
  not not_1 (NOT_BUSY, BUSY);
  Register #(.width(1), .trigger("falling"), .showLabel("true")) u_RESULT_NEGATIVE (
    .D(NEG_RESULT), .en(ACCEPT), .Q(RESULT_NEGATIVE), .clk(CLK), .clr(RESET));
  Comparator #(.width(32), .mode("unsigned")) comparator_1 (.a(B), .b({32{1'b0}}), .eq(DIV_ZERO));  // open: gt, lt
  or or_1 (INITIAL_ERROR, DIV_ZERO, ERROR_INPUT[1]);
  assign DIVISOR_EXT = {{1{1'b0}}, DIVISOR};  // Bit_Extender bit_extender_1
  Multiplexer #(.width(33), .select(1), .enable("false")) multiplexer_1 (
    .in0({R[31:0], Q[31]}), .in1(TRIAL), .out(R_STEP), .sel(ENOUGH));
  Register #(.width(32), .trigger("falling"), .showLabel("true")) u_Q (
    .D(Q_NEXT), .en(STEP_ENABLE), .Q(Q), .clk(CLK), .clr(RESET));
  Multiplexer #(.width(5), .select(1), .enable("false")) multiplexer_2 (
    .in0(COUNT_PLUS), .in1({5{1'b0}}), .out(COUNT_NEXT), .sel(ACCEPT));
  and and_1 (CONTINUE_RUN, BUSY, NOT_LAST);
  or or_2 (FINISH, ERROR_FINISH, ITERATION_FINISH);
  not not_2 (NOT_DONE, DONE);
  Register #(.width(1), .trigger("falling"), .showLabel("true")) u_REMAINDER_NEGATIVE (
    .D(NEG_A), .en(ACCEPT), .Q(REMAINDER_NEGATIVE), .clk(CLK), .clr(RESET));
  Comparator #(.width(32), .mode("unsigned")) comparator_2 (.a(A), .b(32'h80000000), .eq(A_IS_MIN));  // open: gt, lt
  ConditionalNegate32 conditionalnegate32_2 (.VALUE(Q), .NEG(RESULT_NEGATIVE), .RESULT(QUOTIENT_SIGNED));
  Register #(.width(5), .trigger("falling"), .showLabel("true")) u_COUNT (
    .D(COUNT_NEXT), .en(STEP_ENABLE), .Q(COUNT), .clk(CLK), .clr(RESET));
  or or_3 (BUSY_NEXT, BEGIN_RUN, CONTINUE_RUN);
  not not_3 (NOT_ACK, ACK);
  and and_2 (NEG_B, SIGNED, B[31]);
  and and_3 (IDLE, NOT_BUSY, NOT_DONE);
  Comparator #(.width(32), .mode("unsigned")) comparator_3 (
    .a(B), .b({32{1'b1}}), .eq(B_IS_MINUS_ONE));  // open: gt, lt
  Register #(.width(2), .trigger("falling"), .showLabel("true")) u_ERROR (
    .D({ERROR_INPUT[1], DIV_ZERO}), .en(ACCEPT), .Q(ERROR), .clk(CLK), .clr(RESET));
  Multiplexer #(.width(33), .select(1), .enable("false")) multiplexer_3 (
    .in0(R_STEP), .in1({33{1'b0}}), .out(R_NEXT), .sel(ACCEPT));
  ConditionalNegate32 conditionalnegate32_3 (.VALUE(R[31:0]), .NEG(REMAINDER_NEGATIVE), .RESULT(REMAINDER_SIGNED));
  not not_4 (NOT_LAST, LAST);
  Register #(.width(1), .trigger("falling"), .showLabel("true")) u_BUSY (
    .D(BUSY_NEXT), .en(1'b1), .Q(BUSY), .clk(CLK), .clr(RESET));
  and and_4 (HOLD_DONE, DONE, NOT_ACK);
  ConditionalNegate32 conditionalnegate32_4 (.VALUE(B), .NEG(NEG_B), .RESULT(ABS_B));
  and and_5 (ACCEPT, START, IDLE);
  and and_6 (OVERFLOW_PAIR, A_IS_MIN, B_IS_MINUS_ONE);
  Register #(.width(1), .trigger("falling"), .showLabel("true")) u_HAS_ERROR (
    .D(INITIAL_ERROR), .en(ACCEPT), .Q(HAS_ERROR), .clk(CLK), .clr(RESET));
  Multiplexer #(.width(32), .select(1), .enable("false")) multiplexer_4 (
    .in0({Q[30:0], ENOUGH}), .in1(ABS_A), .out(Q_NEXT), .sel(ACCEPT));
  Multiplexer #(.width(32), .select(1), .enable("false")) multiplexer_5 (
    .in0(QUOTIENT_SIGNED), .in1({32{1'b0}}), .out(LO), .sel(HAS_ERROR));
  Comparator #(.width(5), .mode("unsigned")) comparator_4 (.a(COUNT), .b({5{1'b1}}), .eq(LAST));  // open: gt, lt
  not not_5 (NO_INITIAL_ERROR, INITIAL_ERROR);
  and and_7 (ERROR_FINISH, ACCEPT, INITIAL_ERROR);
  or or_4 (DONE_NEXT, FINISH, HOLD_DONE);
  and and_8 (NEG_A, SIGNED, A[31]);
  // XOR_Gate #(.width(1)) xor_1: pin names not known; wires that end beside it: NEG_A, NEG_B, NEG_RESULT
  or or_5 (STEP_ENABLE, ACCEPT, BUSY);
  and and_9 (ERROR_INPUT[1], OVERFLOW_PAIR, SIGNED);
  Register #(.width(32), .trigger("falling"), .showLabel("true")) u_DIVISOR (
    .D(ABS_B), .en(ACCEPT), .Q(DIVISOR), .clk(CLK), .clr(RESET));
  SliceArithmetic33 slicearithmetic33_1 (
    .A({R[31:0], Q[31]}), .B(DIVISOR_EXT), .SUB(1'b1), .RESULT(TRIAL), .CARRY(ENOUGH));
  Register #(.width(33), .trigger("falling"), .showLabel("true")) u_R (
    .D(R_NEXT), .en(STEP_ENABLE), .Q(R), .clk(CLK), .clr(RESET));
  Multiplexer #(.width(32), .select(1), .enable("false")) multiplexer_6 (
    .in0(REMAINDER_SIGNED), .in1({32{1'b0}}), .out(HI), .sel(HAS_ERROR));
  Adder #(.width(5)) adder_1 (.a(COUNT), .b(5'b00001), .out(COUNT_PLUS), .cin(1'b0), .cout(COUNT_WRAP));
  and and_10 (BEGIN_RUN, ACCEPT, NO_INITIAL_ERROR);
  and and_11 (ITERATION_FINISH, BUSY, LAST);
  Register #(.width(1), .trigger("falling"), .showLabel("true")) u_DONE (
    .D(DONE_NEXT), .en(1'b1), .Q(DONE), .clk(CLK), .clr(RESET));

  // Other names for the same wires on the sheet: A_LOW[30:0] = A[30:0]; A_SIGN = A[31]; B_LOW[30:0] = B[30:0];
  //   B_SIGN = B[31]; ERROR_INPUT[0] = DIV_ZERO; SIGNED_OVERFLOW = ERROR_INPUT[1]; Q_SHIFT[31:0] = {Q[30:0], ENOUGH};
  //   Q_LOWER[30:0] = Q[30:0]; R_EXTRA = R[32]; Q_MSB = Q[31]; R_SHIFT[32:0] = {R[31:0], Q[31]};
  //   R_LOWER[31:0] = R[31:0]
endmodule

module Lavaneko (
  output [15:0] PC,
  output [31:0] REG1,
  output [31:0] REG2,
  output [31:0] REG3,
  output [31:0] REG4,
  output Z,
  output C,
  output halt,
  output [31:0] LO,
  output [31:0] HI,
  output [1:0] MD_ERROR,
  output BUSY
);

  wire A_REG, ALU_CARRY, ALU_ZERO, B_ZERO, BRANCH, CLK, CORE_DONE, DIV_BUSY, DIV_DONE, DIV_START, ENABLE,
       FETCH, FLAGS_WRITE, IS_MULTIPLY, JUMP, JZ, LOAD, MD, MD_ACK, MD_DIV, MD_OK, MD_SIGNED, MD_START,
       MEM_WRITE, MUL_BUSY, MUL_DONE, MUL_START, REG_WRITE, RESET, STORE, SUB, WRITE;
  wire [1:0] CORE_ERROR, DEST, DIV_ERROR, MUL_ERROR, SELECT_A, SELECT_B, WB_SELECT;
  wire [15:0] ADDRESS, programcounter_1_pc;
  wire [31:0] addsub_1_result, BASE_WRITEBACK, CORE_HI, CORE_LO, dataram_1_read, DIV_HI, DIV_LO, IMMEDIATE,
       MUL_HI, MUL_LO, multiplexer_1_out, multiplexer_2_out, READ_A, READ_B, READ_LO, STATUS_WORD, WRITEBACK;
  wire [47:0] IR_q, programrom_1_instruction;

  ProgramCounter programcounter_1 (
    .CLK(CLK), .RESET(RESET), .ENABLE(ENABLE), .JUMP(BRANCH), .TARGET(ADDRESS), .PC(programcounter_1_pc));
  Clock #(.highDuration(1), .lowDuration(1)) SYSTEM_TICK (.out(CLK));
  Button u_RESET (.out(RESET));
  ProgramROM programrom_1 (.ADDRESS(programcounter_1_pc), .INSTRUCTION(programrom_1_instruction));
  Register #(.width(48), .trigger("rising"), .showLabel("true")) IR (
    .D(programrom_1_instruction), .en(FETCH), .Q(IR_q), .clk(CLK), .clr(RESET));
  Control control_1 (
    .INSTRUCTION(IR_q), .SUB(SUB), .REG_WRITE(REG_WRITE), .LOAD(LOAD), .STORE(STORE), .JUMP(JUMP),
    .B_ZERO(B_ZERO), .HALT(halt), .A_REG(A_REG), .SELECT_B(SELECT_B), .DEST(DEST), .SELECT_A(SELECT_A),
    .FLAGS_WRITE(FLAGS_WRITE), .JZ(JZ), .IMMEDIATE(IMMEDIATE), .MD(MD), .MD_SIGNED(MD_SIGNED),
    .MD_DIV(MD_DIV), .WB_SELECT(WB_SELECT));
  Sequencer sequencer_1 (
    .CLK(CLK), .RESET(RESET), .HALT(halt), .REG_WRITE(REG_WRITE), .STORE(STORE), .FLAGS_WRITE(FLAGS_WRITE),
    .JUMP(JUMP), .JZ(JZ), .ALU_ZERO(ALU_ZERO), .ALU_CARRY(ALU_CARRY), .MD(MD), .CORE_DONE(CORE_DONE),
    .MD_OK(MD_OK), .ENABLE(ENABLE), .FETCH(FETCH), .WRITE(WRITE), .MEM_WRITE(MEM_WRITE), .BRANCH(BRANCH),
    .Z(Z), .C(C), .BUSY(BUSY), .MD_START(MD_START), .MD_ACK(MD_ACK));
  RegisterBank registerbank_1 (
    .CLK(CLK), .RESET(RESET), .WRITE(WRITE), .DEST(DEST), .SELECT_A(SELECT_A), .SELECT_B(SELECT_B),
    .DATA(WRITEBACK), .READ_A(READ_A), .READ_B(READ_B), .REG1(REG1), .REG2(REG2), .REG3(REG3), .REG4(REG4));
  Bit_Extender #(.in_width(32), .out_width(16), .\type ("zero")) bit_extender_1 (.in(IMMEDIATE), .out(ADDRESS));
  not not_1 (IS_MULTIPLY, MD_DIV);
  and and_1 (MUL_START, MD_START, IS_MULTIPLY);
  and and_2 (DIV_START, MD_START, MD_DIV);
  Multiplexer #(.width(32), .select(1), .enable("false")) multiplexer_1 (
    .in0(IMMEDIATE), .in1(READ_A), .out(multiplexer_1_out), .sel(A_REG));
  Multiplexer #(.width(32), .select(1), .enable("false")) multiplexer_2 (
    .in0(READ_B), .in1({32{1'b0}}), .out(multiplexer_2_out), .sel(B_ZERO));
  AddSub addsub_1 (
    .A(multiplexer_1_out), .B(multiplexer_2_out), .SUB(SUB), .RESULT(addsub_1_result), .CARRY(ALU_CARRY),
    .ZERO(ALU_ZERO));
  MultiplyUnit multiplyunit_1 (
    .CLK(CLK), .RESET(RESET), .START(MUL_START), .ACK(MD_ACK), .SIGNED(MD_SIGNED), .A(READ_A), .B(READ_B),
    .BUSY(MUL_BUSY), .DONE(MUL_DONE), .LO(MUL_LO), .HI(MUL_HI), .ERROR(MUL_ERROR));
  DivideUnit divideunit_1 (
    .CLK(CLK), .RESET(RESET), .START(DIV_START), .ACK(MD_ACK), .SIGNED(MD_SIGNED), .A(READ_A), .B(READ_B),
    .BUSY(DIV_BUSY), .DONE(DIV_DONE), .LO(DIV_LO), .HI(DIV_HI), .ERROR(DIV_ERROR));
  DataRAM dataram_1 (
    .CLK(CLK), .RESET(RESET), .WRITE(MEM_WRITE), .ADDRESS(ADDRESS), .DATA(READ_B), .READ(dataram_1_read));
  Multiplexer #(.width(1), .select(1), .enable("false")) multiplexer_3 (
    .in0(MUL_DONE), .in1(DIV_DONE), .out(CORE_DONE), .sel(MD_DIV));
  Multiplexer #(.width(32), .select(1), .enable("false")) multiplexer_4 (
    .in0(MUL_LO), .in1(DIV_LO), .out(CORE_LO), .sel(MD_DIV));
  Multiplexer #(.width(32), .select(1), .enable("false")) multiplexer_5 (
    .in0(MUL_HI), .in1(DIV_HI), .out(CORE_HI), .sel(MD_DIV));
  Multiplexer #(.width(2), .select(1), .enable("false")) multiplexer_6 (
    .in0(MUL_ERROR), .in1(DIV_ERROR), .out(CORE_ERROR), .sel(MD_DIV));
  Multiplexer #(.width(32), .select(1), .enable("false")) multiplexer_7 (
    .in0(addsub_1_result), .in1(dataram_1_read), .out(BASE_WRITEBACK), .sel(LOAD));
  Multiplexer #(.width(32), .select(1), .enable("false")) multiplexer_8 (
    .in0(LO), .in1(CORE_LO), .out(READ_LO), .sel(MD));
  assign STATUS_WORD = {{30{1'b0}}, MD_ERROR};  // Bit_Extender bit_extender_2
  Register #(.width(32), .trigger("falling"), .showLabel("true")) u_LO (
    .D(CORE_LO), .en(MD_ACK), .Q(LO), .clk(CLK), .clr(RESET));
  Register #(.width(32), .trigger("falling"), .showLabel("true")) u_HI (
    .D(CORE_HI), .en(MD_ACK), .Q(HI), .clk(CLK), .clr(RESET));
  Register #(.width(2), .trigger("falling"), .showLabel("true")) u_MD_ERROR (
    .D(CORE_ERROR), .en(MD_ACK), .Q(MD_ERROR), .clk(CLK), .clr(RESET));
  Comparator #(.width(2), .mode("unsigned")) comparator_1 (.a(CORE_ERROR), .b(2'b00), .eq(MD_OK));  // open: gt, lt
  Multiplexer #(.width(32), .select(2), .enable("false")) multiplexer_9 (
    .in0(BASE_WRITEBACK), .in1(READ_LO), .in2(HI), .in3(STATUS_WORD), .out(WRITEBACK), .sel(WB_SELECT));

  // Notes on the sheet:
  //   LAVANEKO 32
  //   Fetch / decode / operands / execute / memory / writeback
  //   01  PROGRAM COUNTER
  //   Rising edge: fetch   /   Falling edge: execute
  //   02  PROGRAM ROM
  //   03  INSTRUCTION
  //   04  DECODE
  //   CLOCK / COMMIT / BRANCH CONTROL
  //   05  REGISTERS
  //   06  ARITHMETIC
  //   INDEPENDENT MULTIPLY / DIVIDE
  //   07  DATA MEMORY
  //   08  WRITEBACK
endmodule

module CPU_Test (
  input  CLK,
  input  RESET,
  output [15:0] PC,
  output [31:0] REG1,
  output [31:0] REG2,
  output [31:0] REG3,
  output [31:0] REG4,
  output Z,
  output C,
  output halt,
  output [31:0] LO,
  output [31:0] HI,
  output [1:0] MD_ERROR,
  output BUSY
);

  wire A_REG, ALU_CARRY, ALU_ZERO, B_ZERO, BRANCH, CORE_DONE, DIV_BUSY, DIV_DONE, DIV_START, ENABLE, FETCH,
       FLAGS_WRITE, IS_MULTIPLY, JUMP, JZ, LOAD, MD, MD_ACK, MD_DIV, MD_OK, MD_SIGNED, MD_START, MEM_WRITE,
       MUL_BUSY, MUL_DONE, MUL_START, REG_WRITE, STORE, SUB, WRITE;
  wire [1:0] CORE_ERROR, DEST, DIV_ERROR, MUL_ERROR, SELECT_A, SELECT_B, WB_SELECT;
  wire [15:0] ADDRESS, programcounter_1_pc;
  wire [31:0] addsub_1_result, BASE_WRITEBACK, CORE_HI, CORE_LO, dataram_1_read, DIV_HI, DIV_LO, IMMEDIATE,
       MUL_HI, MUL_LO, multiplexer_1_out, multiplexer_2_out, READ_A, READ_B, READ_LO, STATUS_WORD, WRITEBACK;
  wire [47:0] IR_q, programrom_1_instruction;

  ProgramCounter programcounter_1 (
    .CLK(CLK), .RESET(RESET), .ENABLE(ENABLE), .JUMP(BRANCH), .TARGET(ADDRESS), .PC(programcounter_1_pc));
  ProgramROM programrom_1 (.ADDRESS(programcounter_1_pc), .INSTRUCTION(programrom_1_instruction));
  Register #(.width(48), .trigger("rising"), .showLabel("true")) IR (
    .D(programrom_1_instruction), .en(FETCH), .Q(IR_q), .clk(CLK), .clr(RESET));
  Control control_1 (
    .INSTRUCTION(IR_q), .SUB(SUB), .REG_WRITE(REG_WRITE), .LOAD(LOAD), .STORE(STORE), .JUMP(JUMP),
    .B_ZERO(B_ZERO), .HALT(halt), .A_REG(A_REG), .SELECT_B(SELECT_B), .DEST(DEST), .SELECT_A(SELECT_A),
    .FLAGS_WRITE(FLAGS_WRITE), .JZ(JZ), .IMMEDIATE(IMMEDIATE), .MD(MD), .MD_SIGNED(MD_SIGNED),
    .MD_DIV(MD_DIV), .WB_SELECT(WB_SELECT));
  Sequencer sequencer_1 (
    .CLK(CLK), .RESET(RESET), .HALT(halt), .REG_WRITE(REG_WRITE), .STORE(STORE), .FLAGS_WRITE(FLAGS_WRITE),
    .JUMP(JUMP), .JZ(JZ), .ALU_ZERO(ALU_ZERO), .ALU_CARRY(ALU_CARRY), .MD(MD), .CORE_DONE(CORE_DONE),
    .MD_OK(MD_OK), .ENABLE(ENABLE), .FETCH(FETCH), .WRITE(WRITE), .MEM_WRITE(MEM_WRITE), .BRANCH(BRANCH),
    .Z(Z), .C(C), .BUSY(BUSY), .MD_START(MD_START), .MD_ACK(MD_ACK));
  RegisterBank registerbank_1 (
    .CLK(CLK), .RESET(RESET), .WRITE(WRITE), .DEST(DEST), .SELECT_A(SELECT_A), .SELECT_B(SELECT_B),
    .DATA(WRITEBACK), .READ_A(READ_A), .READ_B(READ_B), .REG1(REG1), .REG2(REG2), .REG3(REG3), .REG4(REG4));
  Bit_Extender #(.in_width(32), .out_width(16), .\type ("zero")) bit_extender_1 (.in(IMMEDIATE), .out(ADDRESS));
  not not_1 (IS_MULTIPLY, MD_DIV);
  and and_1 (MUL_START, MD_START, IS_MULTIPLY);
  and and_2 (DIV_START, MD_START, MD_DIV);
  Multiplexer #(.width(32), .select(1), .enable("false")) multiplexer_1 (
    .in0(IMMEDIATE), .in1(READ_A), .out(multiplexer_1_out), .sel(A_REG));
  Multiplexer #(.width(32), .select(1), .enable("false")) multiplexer_2 (
    .in0(READ_B), .in1({32{1'b0}}), .out(multiplexer_2_out), .sel(B_ZERO));
  AddSub addsub_1 (
    .A(multiplexer_1_out), .B(multiplexer_2_out), .SUB(SUB), .RESULT(addsub_1_result), .CARRY(ALU_CARRY),
    .ZERO(ALU_ZERO));
  MultiplyUnit multiplyunit_1 (
    .CLK(CLK), .RESET(RESET), .START(MUL_START), .ACK(MD_ACK), .SIGNED(MD_SIGNED), .A(READ_A), .B(READ_B),
    .BUSY(MUL_BUSY), .DONE(MUL_DONE), .LO(MUL_LO), .HI(MUL_HI), .ERROR(MUL_ERROR));
  DivideUnit divideunit_1 (
    .CLK(CLK), .RESET(RESET), .START(DIV_START), .ACK(MD_ACK), .SIGNED(MD_SIGNED), .A(READ_A), .B(READ_B),
    .BUSY(DIV_BUSY), .DONE(DIV_DONE), .LO(DIV_LO), .HI(DIV_HI), .ERROR(DIV_ERROR));
  DataRAM dataram_1 (
    .CLK(CLK), .RESET(RESET), .WRITE(MEM_WRITE), .ADDRESS(ADDRESS), .DATA(READ_B), .READ(dataram_1_read));
  Multiplexer #(.width(1), .select(1), .enable("false")) multiplexer_3 (
    .in0(MUL_DONE), .in1(DIV_DONE), .out(CORE_DONE), .sel(MD_DIV));
  Multiplexer #(.width(32), .select(1), .enable("false")) multiplexer_4 (
    .in0(MUL_LO), .in1(DIV_LO), .out(CORE_LO), .sel(MD_DIV));
  Multiplexer #(.width(32), .select(1), .enable("false")) multiplexer_5 (
    .in0(MUL_HI), .in1(DIV_HI), .out(CORE_HI), .sel(MD_DIV));
  Multiplexer #(.width(2), .select(1), .enable("false")) multiplexer_6 (
    .in0(MUL_ERROR), .in1(DIV_ERROR), .out(CORE_ERROR), .sel(MD_DIV));
  Multiplexer #(.width(32), .select(1), .enable("false")) multiplexer_7 (
    .in0(addsub_1_result), .in1(dataram_1_read), .out(BASE_WRITEBACK), .sel(LOAD));
  Multiplexer #(.width(32), .select(1), .enable("false")) multiplexer_8 (
    .in0(LO), .in1(CORE_LO), .out(READ_LO), .sel(MD));
  assign STATUS_WORD = {{30{1'b0}}, MD_ERROR};  // Bit_Extender bit_extender_2
  Register #(.width(32), .trigger("falling"), .showLabel("true")) u_LO (
    .D(CORE_LO), .en(MD_ACK), .Q(LO), .clk(CLK), .clr(RESET));
  Register #(.width(32), .trigger("falling"), .showLabel("true")) u_HI (
    .D(CORE_HI), .en(MD_ACK), .Q(HI), .clk(CLK), .clr(RESET));
  Register #(.width(2), .trigger("falling"), .showLabel("true")) u_MD_ERROR (
    .D(CORE_ERROR), .en(MD_ACK), .Q(MD_ERROR), .clk(CLK), .clr(RESET));
  Comparator #(.width(2), .mode("unsigned")) comparator_1 (.a(CORE_ERROR), .b(2'b00), .eq(MD_OK));  // open: gt, lt
  Multiplexer #(.width(32), .select(2), .enable("false")) multiplexer_9 (
    .in0(BASE_WRITEBACK), .in1(READ_LO), .in2(HI), .in3(STATUS_WORD), .out(WRITEBACK), .sel(WB_SELECT));

  // Notes on the sheet:
  //   LAVANEKO 32
  //   Fetch / decode / operands / execute / memory / writeback
  //   01  PROGRAM COUNTER
  //   Rising edge: fetch   /   Falling edge: execute
  //   02  PROGRAM ROM
  //   03  INSTRUCTION
  //   04  DECODE
  //   CLOCK / COMMIT / BRANCH CONTROL
  //   05  REGISTERS
  //   06  ARITHMETIC
  //   INDEPENDENT MULTIPLY / DIVIDE
  //   07  DATA MEMORY
  //   08  WRITEBACK
endmodule
